// Logisim project Guess The Number XTREME (Arthut&Renan&Pablo).circ as structural Verilog: 9 circuits, main circuit Unidades e Dezenas
module Somador (
  input  [3:0] in_1,
  input  [3:0] in_2,
  output [4:0] out_3
);

  Adder #(.width(4)) adder_1 (.a(in_1), .b(in_2), .out(out_3[3:0]), .cout(out_3[4]));  // open: cin
endmodule

module \Diferença  (
  input  [4:0] in_1,
  input  [4:0] in_2,
  output [4:0] out_3
);

  wire comparator_1_gt, comparator_1_lt;
  wire [1:0] and_1_out, bit_extender_1_out, bit_extender_2_out;
  wire [4:0] subtractor_1_out, subtractor_2_out;

  Subtractor #(.width(5)) subtractor_1 (.a(in_1), .b(in_2), .out(subtractor_1_out));  // open: bin, bout
  Subtractor #(.width(5)) subtractor_2 (.a(in_2), .b(in_1), .out(subtractor_2_out));  // open: bin, bout
  Comparator #(.width(5), .mode("unsigned")) comparator_1 (
    .a(in_2), .b(in_1), .gt(comparator_1_gt), .lt(comparator_1_lt));  // open: eq
  Multiplexer #(.select(2), .width(5), .enable("false")) multiplexer_1 (
    .in0(subtractor_1_out), .in1(subtractor_2_out), .out(out_3), .sel(and_1_out));  // open: in2, in3
  assign and_1_out = bit_extender_1_out & ~bit_extender_2_out;  // AND_Gate and_1, 2 bits wide
  assign bit_extender_1_out = {{1{1'b0}}, comparator_1_gt};  // Bit_Extender bit_extender_1
  assign bit_extender_2_out = {{1{1'b0}}, comparator_1_lt};  // Bit_Extender bit_extender_2
endmodule

module Cores (
  input  [4:0] in_1,
  output [7:0] red,
  output [7:0] blue
);

  assign red = ~{in_1, 3'b111};  // NOT_Gate not_1, 8 bits wide

  assign blue = {in_1, 3'b111};
endmodule

module Extensor_de_1_p__8_bits (
  input  in_1,
  output [7:0] out_2
);


  assign out_2 = {8{in_1}};
endmodule

module Extensor_de_1_p__4_bits (
  input  in_1,
  output [3:0] out_2
);


  assign out_2 = {4{in_1}};
endmodule

module Unidades_e_Dezenas (
  input  Minutos_D,
  input  Segundos_D,
  input  Minutos_U,
  input  Segundo_U,
  input  CLK,
  input  \config ,
  input  in_7,
  output PARE,
  output [3:0] out_9,
  output [3:0] out_10,
  output [3:0] out_11,
  output [3:0] out_12
);

  wire _01, _02, _03, _04, and_1_out, and_2_out, and_3_out, and_5_out, and_6_out, and_7_out, comparator_1_eq,
       comparator_2_eq, comparator_3_eq, counter_1_q, counter_2_q, counter_5_q, or_1_out, or_2_out, or_3_out,
       or_4_out;

  Comparator #(.width(4)) comparator_1 (.a(out_11), .b(4'b0101), .eq(comparator_1_eq));  // open: gt, lt
  Comparator #(.width(4)) comparator_2 (.a(out_10), .b(4'b1001), .eq(comparator_2_eq));  // open: gt, lt
  Counter #(.width(1), .max('h1)) counter_1 (
    .Q(counter_1_q), .clk(comparator_1_eq), .clr(counter_1_q));  // open: load, D, count, carry, preset, down
  Counter #(.width(1), .max('h1)) counter_2 (
    .Q(counter_2_q), .clk(comparator_2_eq), .clr(counter_2_q));  // open: load, D, count, carry, preset, down
  and and_1 (and_1_out, counter_1_q, ~\config , ~PARE);  // AND_Gate
  and and_2 (and_2_out, Minutos_D, \config );
  or or_1 (or_1_out, and_2_out, counter_2_q);
  and and_3 (and_3_out, Minutos_U, \config );
  or or_2 (or_2_out, and_3_out, and_1_out);
  Hex_Digit_Display hex_digit_display_1 (.value(out_9));  // open: dp
  Hex_Digit_Display hex_digit_display_2 (.value(out_10));  // open: dp
  Counter #(.width(4), .max('h5)) counter_3 (
    .Q(out_9), .carry(_04), .clk(or_1_out), .clr(in_7), .down(1'b1));  // open: load, D, count, preset
  Counter #(.width(4), .max('h9)) counter_4 (
    .Q(out_10), .carry(_03), .clk(or_2_out), .clr(in_7), .down(1'b1));  // open: load, D, count, preset
  and and_4 (PARE, _04, _03, _02, _01);
  Comparator #(.width(4)) comparator_3 (.a(out_12), .b(4'b1001), .eq(comparator_3_eq));  // open: gt, lt
  Counter #(.width(1), .max('h1)) counter_5 (
    .Q(counter_5_q), .clk(comparator_3_eq), .clr(counter_5_q));  // open: load, D, count, carry, preset, down
  and and_5 (and_5_out, Segundos_D, \config );
  and and_6 (and_6_out, CLK, ~\config , ~PARE);  // AND_Gate
  or or_3 (or_3_out, and_5_out, counter_5_q);
  and and_7 (and_7_out, Segundo_U, \config );
  or or_4 (or_4_out, and_7_out, and_6_out);
  Hex_Digit_Display hex_digit_display_3 (.value(out_11));  // open: dp
  Hex_Digit_Display hex_digit_display_4 (.value(out_12));  // open: dp
  Counter #(.width(4), .max('h5)) counter_6 (
    .Q(out_11), .carry(_02), .clk(or_3_out), .clr(in_7), .down(1'b1));  // open: load, D, count, preset
  Counter #(.width(4), .max('h9)) counter_7 (
    .Q(out_12), .carry(_01), .clk(or_4_out), .clr(in_7), .down(1'b1));  // open: load, D, count, preset

  // Other names for the same wires on the sheet: _1abaixar[3:0] = out_10; _3abaixar[3:0] = out_11;
  //   abaixar[3:0] = out_12; Reset = in_7
endmodule

module Gtx_Adaptador (
  input  ALguem_marcou,
  input  Colocar_o_Chute,
  input  Confirmar,
  input  \Avançar ,
  input  Resey,
  output [3:0] X_Atual,
  output [3:0] Y_Atual,
  output X_Certo,
  output Y_Certo,
  output Soma_Certa,
  output [7:0] RED,
  output [3:0] \Qual_Nº ,
  output [7:0] BLUE,
  output X_Jognado,
  output Y_jogando
);

  wire and_1_out, and_2_out, and_3_out, and_4_out, ATIVADOR, \Avançar_2 , Chute_X_Nao, comparator_3_eq,
       comparator_4_eq, comparator_5_eq, counter_2_q, or_1_out, or_2_out, or_3_out, or_4_out, or_5_out, Sinal;
  wire [1:0] counter_4_q;
  wire [3:0] Chute_X, Chute_Y, \Nº_X_Aleatorio , \Nº_Y_Aleatorio , x, y;
  wire [4:0] \diferença_1_out_3 , Soma_Aleatoria, Soma_do_Chute;
  wire [7:0] cores_1_blue, cores_1_red, extensor_de_1_p_8_bits_1_out_2;

  Counter #(.width(1), .max('h1)) counter_1 (
    .Q(Chute_X_Nao), .clk(Confirmar), .clr(\Avançar ));  // open: load, D, count, carry, preset, down
  and and_1 (and_1_out, Confirmar, counter_2_q);
  Counter #(.width(1), .max('h1)) counter_2 (
    .Q(counter_2_q), .clk(Y_jogando), .clr(Sinal));  // open: load, D, count, carry, preset, down
  or or_1 (or_1_out, Resey, ALguem_marcou);
  Random random_1 (.clk(or_1_out), .out({\Nº_Y_Aleatorio , \Nº_X_Aleatorio }));  // open: next, clr
  Counter #(.width(1), .max('h1)) counter_3 (
    .Q(Sinal), .clk(and_1_out), .clr(\Avançar_2 ));  // open: load, D, count, carry, preset, down
  Counter #(.width(2), .max('h3)) counter_4 (
    .Q(counter_4_q), .clk(\Avançar ), .clr(\Avançar_2 ));  // open: load, D, count, carry, preset, down
  Somador somador_1 (.in_1(\Nº_X_Aleatorio ), .in_2(\Nº_Y_Aleatorio ), .out_3(Soma_Aleatoria));
  Comparator #(.width(2), .mode("unsigned")) comparator_1 (
    .a(counter_4_q), .b(2'b10), .eq(\Avançar_2 ));  // open: gt, lt
  Register #(.width(4), .trigger("high"), .Select("low")) register_1 (
    .D(Chute_X), .Q(X_Atual), .clk(Confirmar), .clr(or_2_out));  // open: en
  or or_2 (or_2_out, \Avançar_2 , Resey);
  Register #(.width(4), .Select("low")) register_2 (.D(x), .Q(Chute_X), .clk(and_2_out), .clr(or_3_out));  // open: en
  and and_2 (and_2_out, ~ATIVADOR, Confirmar);  // AND_Gate
  or or_3 (or_3_out, \Avançar_2 , Resey);
  Somador somador_2 (.in_1(Chute_X), .in_2(Chute_Y), .out_3(Soma_do_Chute));
  Counter #(.width(4), .max('hf)) counter_5 (
    .Q(\Qual_Nº ), .clk(and_3_out), .clr(\Avançar ));  // open: load, D, count, carry, preset, down
  and and_3 (and_3_out, ~Chute_X_Nao, ~Sinal, Colocar_o_Chute);  // AND_Gate
  Register #(.width(4), .trigger("high"), .Select("low")) register_3 (
    .D(Chute_Y), .Q(Y_Atual), .clk(Confirmar), .clr(or_4_out));  // open: en
  or or_4 (or_4_out, \Avançar_2 , Resey);
  and and_4 (and_4_out, ATIVADOR, Confirmar);
  Demultiplexer #(.width(4), .enable("false")) demultiplexer_1 (.out0(x), .out1(y), .in(\Qual_Nº ), .sel(ATIVADOR));
  Counter #(.width(1), .max('h1)) counter_6 (
    .Q(ATIVADOR), .clk(\Avançar ), .clr(\Avançar_2 ));  // open: load, D, count, carry, preset, down
  Register #(.width(4), .Select("low")) register_4 (.D(y), .Q(Chute_Y), .clk(and_4_out), .clr(or_5_out));  // open: en
  or or_5 (or_5_out, \Avançar_2 , Resey);
  Comparator #(.width(1)) comparator_2 (.a(ATIVADOR), .b(1'b0), .eq(X_Jognado), .lt(Y_jogando));  // open: gt
  \Diferença  \diferença_1  (.in_1(Soma_Aleatoria), .in_2(Soma_do_Chute), .out_3(\diferença_1_out_3 ));
  Cores cores_1 (.in_1(\diferença_1_out_3 ), .red(cores_1_red), .blue(cores_1_blue));
  Comparator #(.width(4)) comparator_3 (.a(\Nº_X_Aleatorio ), .b(Chute_X), .eq(comparator_3_eq));  // open: gt, lt
  Comparator #(.width(4)) comparator_4 (.a(\Nº_Y_Aleatorio ), .b(Chute_Y), .eq(comparator_4_eq));  // open: gt, lt
  Comparator #(.width(5)) comparator_5 (.a(Soma_Aleatoria), .b(Soma_do_Chute), .eq(comparator_5_eq));  // open: gt, lt
  Extensor_de_1_p__8_bits extensor_de_1_p_8_bits_1 (.in_1(Sinal), .out_2(extensor_de_1_p_8_bits_1_out_2));
  and and_5 (X_Certo, Sinal, comparator_3_eq);
  and and_6 (Y_Certo, Sinal, comparator_4_eq);
  and and_7 (Soma_Certa, Sinal, comparator_5_eq);
  assign RED = extensor_de_1_p_8_bits_1_out_2 & cores_1_red;  // AND_Gate and_8, 8 bits wide
  assign BLUE = cores_1_blue & extensor_de_1_p_8_bits_1_out_2;  // AND_Gate and_9, 8 bits wide
  // RGBLed #(.multibit("true")) rgbled_1: pin names not known; wires that end beside it: RED, BLUE

  // Other names for the same wires on the sheet: Avança_1 = \Avançar ; Reset = Resey; Sinal_Y = Y_jogando

  // Notes on the sheet:
  //   Depois de Confirma Y ele diz o resultado
  //   Número Aleatorio
  //   Palpite X/Y
  //   SOMANDO X e Y
  //   ARMAZENANDO O CHUTE X e Y
  //   VERIFICADOR SER ACERTOU X, Y ou SOMA
  //   SISTEMA DE CORES DE PERTO OU LONGE
endmodule

module Core (
  input  in_1,
  input  in_2,
  input  in_3,
  input  in_4,
  input  RESET,
  input  START,
  input  C_A,
  input  C_B,
  input  Av__A,
  input  Av__B,
  input  Chute,
  output FIM_DE_JOGO,
  output Jogador_A,
  output Jogador_B,
  output X_Certo,
  output Y_Certo,
  output [3:0] X_Atual,
  output [3:0] Y_Atual,
  output [3:0] Mostra_Chute_A,
  output [3:0] Mostra_Chute_B,
  output A_Venceu,
  output SOMA_C,
  output [3:0] A,
  output OK,
  output out_25,
  output [3:0] M1a,
  output [3:0] M0a,
  output [3:0] S1a,
  output [3:0] S0a,
  output [3:0] M1b,
  output [3:0] M0a_2,
  output [3:0] S1b,
  output [3:0] S0b,
  output out_34,
  output [3:0] B,
  output B_Venceu,
  output Jogando_Y,
  output Jogando_X,
  output [7:0] REd,
  output [7:0] Blue,
  output cfg,
  output jogador__a,
  output JOGADOR_B_2
);

  wire and_1_out, and_2_out, and_6_out, and_7_out, and_9_out, and_10_out, and_15_out, and_16_out, and_17_out,
       and_18_out, and_19_out, and_24_out, and_26_out, \Avançar , clock_1_out, clock_2_out, comparator_2_eq,
       comparator_2_gt, comparator_2_lt, comparator_3_eq, comparator_4_eq, Confirma, counter_1_q,
       counter_2_q, counter_4_q, counter_7_q, counter_8_q, demultiplexer_1_out0, demultiplexer_1_out1,
       gtx_adaptador_1_x_jognado, gtx_adaptador_1_y_jogando, or_1_out, or_2_out, or_3_out, or_4_out,
       or_5_out, or_8_out, PARE_A, PARE_B, SINAl_de_Troca;
  wire [1:0] counter_3_q;
  wire [3:0] extensor_de_1_p_4_bits_1_out_2, extensor_de_1_p_4_bits_2_out_2, Mostra_Chute;

  and and_1 (and_1_out, X_Certo, Y_Certo);
  and and_2 (and_2_out, X_Certo, Y_Certo);
  Counter #(.width(1), .max('h1)) counter_1 (
    .Q(counter_1_q), .clk(and_1_out), .clr(counter_1_q));  // open: load, D, count, carry, preset, down
  Counter #(.width(1), .max('h1)) counter_2 (
    .Q(counter_2_q), .clk(and_2_out), .clr(counter_2_q));  // open: load, D, count, carry, preset, down
  Counter #(.width(2), .max('h2)) counter_3 (
    .Q(counter_3_q), .clk(\Avançar ), .clr(SINAl_de_Troca));  // open: load, D, count, carry, preset, down
  and and_3 (out_25, counter_1_q, jogador__a);
  and and_4 (out_34, counter_2_q, Jogador_B);
  and and_5 (Confirma, ~FIM_DE_JOGO, or_1_out);  // AND_Gate
  or or_1 (or_1_out, and_7_out, and_6_out);
  and and_6 (and_6_out, C_B, Jogador_B);
  and and_7 (and_7_out, jogador__a, C_A);
  Demultiplexer #(.enable("false")) demultiplexer_1 (
    .out0(demultiplexer_1_out0), .out1(demultiplexer_1_out1), .in(1'b1), .sel(counter_4_q));
  Counter #(.width(1), .max('h1)) counter_4 (
    .Q(counter_4_q), .clk(SINAl_de_Troca), .clr(RESET));  // open: load, D, count, carry, preset, down
  Comparator #(.width(2)) comparator_1 (.a(counter_3_q), .b(2'b10), .eq(SINAl_de_Troca));  // open: gt, lt
  and and_8 (\Avançar , ~FIM_DE_JOGO, or_2_out);  // AND_Gate
  or or_2 (or_2_out, and_9_out, and_10_out);
  and and_9 (and_9_out, jogador__a, Av__A);
  and and_10 (and_10_out, Av__B, Jogador_B);
  or or_3 (or_3_out, PARE_B, demultiplexer_1_out0);
  or or_4 (or_4_out, demultiplexer_1_out1, PARE_A);
  Counter #(.width(4), .max('he)) counter_5 (
    .Q(A), .clk(out_25), .clr(RESET));  // open: load, D, count, carry, preset, down
  Counter #(.width(4), .max('he)) counter_6 (
    .Q(B), .clk(out_34), .clr(RESET));  // open: load, D, count, carry, preset, down
  and and_11 (jogador__a, ~PARE_A, or_3_out);  // AND_Gate
  and and_12 (Jogador_B, or_4_out, ~PARE_B);  // AND_Gate
  Comparator #(.width(4), .mode("unsigned")) comparator_2 (
    .a(A), .b(B), .gt(comparator_2_gt), .eq(comparator_2_eq), .lt(comparator_2_lt));
  and and_13 (Jogando_X, ~cfg, gtx_adaptador_1_x_jognado);  // AND_Gate
  and and_14 (Jogando_Y, ~cfg, gtx_adaptador_1_y_jogando);  // AND_Gate
  and and_15 (and_15_out, \Avançar , counter_7_q);
  or or_5 (or_5_out, out_25, out_34);
  Extensor_de_1_p__4_bits extensor_de_1_p_4_bits_1 (.in_1(jogador__a), .out_2(extensor_de_1_p_4_bits_1_out_2));
  Extensor_de_1_p__4_bits extensor_de_1_p_4_bits_2 (.in_1(Jogador_B), .out_2(extensor_de_1_p_4_bits_2_out_2));
  Comparator #(.width(4), .mode("unsigned")) comparator_3 (.a(4'b1110), .b(A), .eq(comparator_3_eq));  // open: gt, lt
  and and_16 (and_16_out, PARE_A, comparator_2_eq, PARE_B);
  Comparator #(.width(4), .mode("unsigned")) comparator_4 (.a(B), .b(4'b1110), .eq(comparator_4_eq));  // open: gt, lt
  Counter #(.width(1), .max('h1)) counter_7 (
    .Q(counter_7_q), .clk(or_5_out), .clr(and_15_out));  // open: load, D, count, carry, preset, down
  or or_6 (A_Venceu, comparator_3_eq, and_17_out);
  and and_17 (and_17_out, PARE_A, comparator_2_gt, PARE_B);
  and and_18 (and_18_out, PARE_A, comparator_2_lt, PARE_B);
  or or_7 (B_Venceu, comparator_4_eq, and_18_out);
  Gtx_Adaptador gtx_adaptador_1 (
    .X_Certo(X_Certo), .Y_Certo(Y_Certo), .Soma_Certa(SOMA_C), .RED(REd), .BLUE(Blue), .\Avançar (\Avançar ),
    .X_Atual(X_Atual), .Y_Atual(Y_Atual), .Colocar_o_Chute(and_19_out), .Confirmar(Confirma),
    .\Qual_Nº (Mostra_Chute), .X_Jognado(gtx_adaptador_1_x_jognado), .Y_jogando(gtx_adaptador_1_y_jogando),
    .Resey(RESET), .ALguem_marcou(and_15_out));
  and and_19 (and_19_out, ~cfg, Chute);  // AND_Gate
  assign Mostra_Chute_A = Mostra_Chute & extensor_de_1_p_4_bits_1_out_2;  // AND_Gate and_20, 4 bits wide
  assign Mostra_Chute_B = extensor_de_1_p_4_bits_2_out_2 & Mostra_Chute;  // AND_Gate and_21, 4 bits wide
  and and_22 (OK, ~cfg, and_16_out);  // AND_Gate
  or or_8 (or_8_out, comparator_3_eq, and_16_out, comparator_4_eq);
  and and_23 (FIM_DE_JOGO, or_8_out, ~cfg);  // AND_Gate
  and and_24 (and_24_out, clock_1_out, jogador__a, ~FIM_DE_JOGO);  // AND_Gate
  Clock clock_1 (.out(clock_1_out));
  Unidades_e_Dezenas unidades_e_dezenas_1 (
    .out_11(S1a), .Segundos_D(in_3), .Segundo_U(in_4), .CLK(and_24_out), .\config (cfg), .out_9(M1a),
    .Minutos_D(in_1), .Minutos_U(in_2), .out_12(S0a), .out_10(M0a), .PARE(PARE_A), .in_7(RESET));
  Counter #(.width(1), .max('h1)) counter_8 (
    .Q(counter_8_q), .clk(START), .clr(RESET));  // open: load, D, count, carry, preset, down
  and and_25 (cfg, ~counter_8_q, 1'b1);  // AND_Gate
  and and_26 (and_26_out, clock_2_out, Jogador_B, ~FIM_DE_JOGO);  // AND_Gate
  Clock clock_2 (.out(clock_2_out));
  Unidades_e_Dezenas unidades_e_dezenas_2 (
    .out_11(S1b), .Segundos_D(in_3), .Segundo_U(in_4), .CLK(and_26_out), .\config (cfg), .out_9(M1b),
    .Minutos_D(in_1), .Minutos_U(in_2), .out_12(S0b), .out_10(M0a_2), .PARE(PARE_B), .in_7(RESET));

  assign Jogador_A = jogador__a;
  assign JOGADOR_B_2 = Jogador_B;

  // Other names for the same wires on the sheet: Alguem_marcou_A = out_25; Alguem_Marcou_B = out_34;
  //   Alguem_vence = FIM_DE_JOGO; Config = cfg; Jogandor_A = jogador__a; Jogandor_B = Jogador_B; m0a_t = in_2;
  //   m1a_t = in_1; s0a_t = in_4; s1a_t = in_3; X = X_Certo; y = Y_Certo

  // Notes on the sheet:
  //   SISTEMA DE PLACAR E LEDS
  //   GTX + CONFIRMAR E AVANÇAR
  //   SISTEMA DE TROCA DE JOGADORES
  //   SISTEMA DO CRONOMETRO 
  //   O START, RESET E E CONFIG
endmodule

module JOGUINHO_BOM (
);

  wire A_venceu, Av_A, Av_B, B_venceu, C_A, C_B, cfg, CHUTE_A, CHUTE_B, core_1_p18, core_1_p21, core_1_p24,
       core_1_p27, Empate, Fim_de_Jogo, Jogador_A, Jogador_A_t, Jogador_B, Jogandor_A, Jogandor_B,
       Jogandor_X, Jogandor_Y, m0a_t, m0b_t, m1a_t, m1b_t, or_1_out, Reset, rgbled_1_p1, rgbled_1_p4, s0a_t,
       s0b_t, s1a_t, s1b_t, Soma_C, Start, tunnel, tunnel_t, X_Certo, Y_Certo;
  wire [3:0] A, B, M0a, M0b, M1a, M1b, Mostra_Chute_A, Mostra_Chute_B, S0a, S0b, S1a, S1b, X_Atual, Y_Atual;
  wire [7:0] b_t, r;

  Hex_Digit_Display hex_digit_display_1 (.value(M1a));  // open: dp
  Hex_Digit_Display hex_digit_display_2 (.value(M0a));  // open: dp
  Button button_1 (.out(m0a_t));
  Button button_2 (.out(m1a_t));
  Button button_3 (.out(CHUTE_A));
  Hex_Digit_Display hex_digit_display_3 (.value(A));  // open: dp
  Hex_Digit_Display hex_digit_display_4 (.value(S1a));  // open: dp
  Button button_4 (.out(s1a_t));
  Hex_Digit_Display hex_digit_display_5 (.value(Mostra_Chute_A));  // open: dp
  Button button_5 (.out(C_A));
  LED led_1 (.in(Jogador_A_t));
  LED led_2 (.in(tunnel));
  Hex_Digit_Display hex_digit_display_6 (.value(S0a));  // open: dp
  Button button_6 (.out(s0a_t));
  Button button_7 (.out(Av_A));
  LED led_3 (.in(X_Certo));
  or or_1 (or_1_out, CHUTE_A, CHUTE_B);
  LED led_4 (.in(A_venceu));
  LED led_5 (.in(Soma_C));
  Hex_Digit_Display hex_digit_display_7 (.value(X_Atual));  // open: dp
  LED led_6 (.in(Jogandor_X));
  Button button_8 (.out(Start));
  // Core core_1: pin names not known; wires that end beside it: Jogandor_X, Jogandor_Y, C_A, C_B, Av_A, Av_B, or_1_out, r, Reset, b_t, Jogador_B, A, Jogador_A, B, X_Atual, Y_Atual, A_venceu, core_1_p18, Empate, B_venceu, core_1_p21, Fim_de_Jogo, M1a, core_1_p24, M0a, S1a, core_1_p27, S0a, M1b, tunnel, M0b, tunnel_t, S1b, S0b, Start, Jogandor_A, Jogandor_B, Mostra_Chute_A, Mostra_Chute_B, X_Certo, Y_Certo, Soma_C, cfg
  LED led_7 (.in(Fim_de_Jogo));
  LED led_8 (.in(Empate));
  LED led_9 (.in(cfg));
  or or_2 (core_1_p21, m0a_t, m0b_t);
  or or_3 (core_1_p18, m1a_t, m1b_t);
  LED led_10 (.in(B_venceu));
  // RGBLed #(.multibit("true")) rgbled_1: pin names not known; wires that end beside it: rgbled_1_p1, r, b_t, rgbled_1_p4
  Hex_Digit_Display hex_digit_display_8 (.value(Y_Atual));  // open: dp
  LED led_11 (.in(Jogandor_Y));
  Button button_9 (.out(Reset));
  or or_4 (core_1_p24, s1a_t, s1b_t);
  or or_5 (core_1_p27, s0a_t, s0b_t);
  LED led_12 (.in(Y_Certo));
  Hex_Digit_Display hex_digit_display_9 (.value(M1b));  // open: dp
  LED led_13 (.in(tunnel_t));
  Hex_Digit_Display hex_digit_display_10 (.value(B));  // open: dp
  Hex_Digit_Display hex_digit_display_11 (.value(M0b));  // open: dp
  Button button_10 (.out(m0b_t));
  Button button_11 (.out(m1b_t));
  Hex_Digit_Display hex_digit_display_12 (.value(Mostra_Chute_B));  // open: dp
  Button button_12 (.out(CHUTE_B));
  Button button_13 (.out(C_B));
  LED led_14 (.in(Jogador_B));
  Hex_Digit_Display hex_digit_display_13 (.value(S1b));  // open: dp
  Hex_Digit_Display hex_digit_display_14 (.value(S0b));  // open: dp
  Button button_14 (.out(s0b_t));
  Button button_15 (.out(s1b_t));
  Button button_16 (.out(Av_B));

  // Notes on the sheet:
  //   +
endmodule
