// Logisim project Adivinha o Número(Arthur&Pablo).circ as structural Verilog
module Display (
  input  in_1,
  input  [3:0] in_2
);

  wire button_1_out, circuito_display_1_a, circuito_display_1_b, circuito_display_1_c, circuito_display_1_d,
       circuito_display_1_e, circuito_display_1_f, circuito_display_1_g, guess_1_out_4;

  Guess guess_1 (.in_1(in_1), .in_2(button_1_out), .Chute(in_2), .out_4(guess_1_out_4));  // open: Red, Blue
  Button button_1 (.out(button_1_out));
  LED led_1 (.in(guess_1_out_4));
  // RGBLed #(.multibit("true")) rgbled_1: pin names not known
  _7_Segment_Display u_7_segment_display_1 (
    .g(circuito_display_1_g), .f(circuito_display_1_f), .a(circuito_display_1_a), .b(circuito_display_1_b),
    .e(circuito_display_1_e), .d(circuito_display_1_d), .c(circuito_display_1_c));  // open: dp
  Circuito_Display circuito_display_1 (
    .A(circuito_display_1_a), .B(circuito_display_1_b), .C(circuito_display_1_c), .D(circuito_display_1_d),
    .E(circuito_display_1_e), .F(circuito_display_1_f), .G(circuito_display_1_g), .in_1(in_2));
endmodule

module Circuito_Display (
  input  [3:0] in_1,
  output A,
  output B,
  output C,
  output D,
  output E,
  output F,
  output G
);

  Circuito_A u_A (.out_5(A), .A(in_1[3]), .B(in_1[2]), .C(in_1[1]), .D(in_1[0]));
  Circuito_B u_B (.out_5(B), .A(in_1[3]), .B(in_1[2]), .C(in_1[1]), .D(in_1[0]));
  Circuito_C u_C (.out_5(C), .A(in_1[3]), .B(in_1[2]), .C(in_1[1]), .D(in_1[0]));
  Circuito_D u_D (.out_5(D), .A(in_1[3]), .B(in_1[2]), .C(in_1[1]), .D(in_1[0]));
  Circuito_E u_E (.out_5(E), .A(in_1[3]), .B(in_1[2]), .C(in_1[1]), .D(in_1[0]));
  Circuito_F u_F (.out_5(F), .A(in_1[3]), .B(in_1[2]), .C(in_1[1]), .D(in_1[0]));
  Circuito_G u_G (.out_5(G), .A(in_1[3]), .B(in_1[2]), .C(in_1[1]), .D(in_1[0]));
endmodule

module Guess (
  input  in_1,
  input  in_2,
  input  [3:0] Chute,
  output out_4,
  output [7:0] Red,
  output [7:0] Blue
);

  wire comparador_de_magnitude_1_a___b_2;
  wire [3:0] \diferença_1_out_3 , random_1_out;
  wire [7:0] as_1_blue, as_1_red, n1_a_8_bits_1_out_2;

  _1_a_8_bits u_1_a_8_bits_1 (.out_2(n1_a_8_bits_1_out_2), .in_1(in_1));
  Random #(.width(4)) random_1 (.clk(in_2), .out(random_1_out));  // open: next, clr
  \Diferença  \diferença_1  (.A(random_1_out), .B(Chute), .out_3(\diferença_1_out_3 ));
  Comparador_de_Magnitude comparador_de_magnitude_1 (
    .A(random_1_out), .B(Chute), .A___B_2(comparador_de_magnitude_1_a___b_2));  // open: A___B, A___B_3
  assign Red = as_1_red & n1_a_8_bits_1_out_2;  // AND_Gate and_1, 8 bits wide
  as as_1 (.Red(as_1_red), .in_1(\diferença_1_out_3 ), .Blue(as_1_blue));
  assign Blue = n1_a_8_bits_1_out_2 & as_1_blue;  // AND_Gate and_2, 8 bits wide
  and and_3 (out_4, in_1, comparador_de_magnitude_1_a___b_2);
endmodule

module as (
  input  [3:0] in_1,
  output [7:0] Red,
  output [7:0] Blue
);

  _1_a_4_bits u_1_a_4_bits_1 (.out_2(Red[3:0]), .in_1(1'b1));
  // RGBLed #(.multibit("true")) rgbled_1: pin names not known
  assign Red[7:4] = ~in_1;  // NOT_Gate not_1, 4 bits wide
  _1_a_4_bits u_1_a_4_bits_2 (.out_2(Blue[3:0]), .in_1(1'b0));

  assign Blue[7:4] = in_1;
endmodule

module Circuito_A (
  input  A,
  input  B,
  input  C,
  input  D,
  output out_5
);

  wire and_1_out, and_2_out, and_3_out, and_4_out, and_5_out, and_6_out;

  and and_1 (and_1_out, B, C);
  and and_2 (and_2_out, ~A, C);  // AND_Gate
  and and_3 (and_3_out, ~A, B, D);  // AND_Gate
  and and_4 (and_4_out, A, ~B, ~C);  // AND_Gate
  and and_5 (and_5_out, A, ~D);  // AND_Gate
  and and_6 (and_6_out, ~B, ~D);  // AND_Gate
  or or_1 (out_5, and_1_out, and_2_out, and_3_out, and_4_out, and_5_out, and_6_out);

  // Notes on the sheet:
  //   FEITO POR ARTHUR
endmodule

module Circuito_B (
  input  A,
  input  B,
  input  C,
  input  D,
  output out_5
);

  wire and_1_out, and_2_out, and_3_out, and_4_out, and_5_out;

  and and_1 (and_1_out, ~B, ~D);  // AND_Gate
  and and_2 (and_2_out, ~A, ~B);  // AND_Gate
  and and_3 (and_3_out, ~A, ~C, ~D);  // AND_Gate
  and and_4 (and_4_out, ~A, C, D);  // AND_Gate
  and and_5 (and_5_out, A, ~C, D);  // AND_Gate
  or or_1 (out_5, and_1_out, and_2_out, and_3_out, and_4_out, and_5_out);

  // Notes on the sheet:
  //   FEITO POR ARTHUR
endmodule

module Circuito_C (
  input  A,
  input  B,
  input  C,
  input  D,
  output out_5
);

  wire and_1_out, and_2_out, and_3_out, and_4_out, and_5_out;

  and and_1 (and_1_out, A, ~B, C);  // AND_Gate
  and and_2 (and_2_out, ~A, C, D);  // AND_Gate
  and and_3 (and_3_out, A, ~C, D);  // AND_Gate
  and and_4 (and_4_out, ~B, ~C);  // AND_Gate
  and and_5 (and_5_out, ~A, B);  // AND_Gate
  or or_1 (out_5, and_1_out, and_2_out, and_3_out, and_4_out, and_5_out);

  // Notes on the sheet:
  //   FEITO POR ARTHUR
endmodule

module Circuito_D (
  input  A,
  input  B,
  input  C,
  input  D,
  output out_5
);

  wire and_1_out, and_2_out, and_3_out, and_4_out, and_5_out;

  and and_1 (and_1_out, ~A, ~B, ~D);  // AND_Gate
  and and_2 (and_2_out, ~B, C, D);  // AND_Gate
  and and_3 (and_3_out, B, C, ~D);  // AND_Gate
  and and_4 (and_4_out, A, ~C);  // AND_Gate
  and and_5 (and_5_out, B, ~C, D);  // AND_Gate
  or or_1 (out_5, and_1_out, and_2_out, and_3_out, and_4_out, and_5_out);

  // Notes on the sheet:
  //   FEITO POR ARTHUR
endmodule

module Circuito_E (
  input  A,
  input  B,
  input  C,
  input  D,
  output out_5
);

  wire and_1_out, and_2_out, and_3_out, and_4_out;

  and and_1 (and_1_out, ~B, ~C, ~D);  // AND_Gate
  and and_2 (and_2_out, A, B);
  and and_3 (and_3_out, A, C);
  and and_4 (and_4_out, C, ~D);  // AND_Gate
  or or_1 (out_5, and_1_out, and_2_out, and_3_out, and_4_out);
endmodule

module Circuito_F (
  input  A,
  input  B,
  input  C,
  input  D,
  output out_5
);

  wire and_1_out, and_2_out, and_3_out, and_4_out, and_5_out, and_6_out;

  and and_1 (and_1_out, ~B, ~C, ~D);  // AND_Gate
  and and_2 (and_2_out, A, ~C, ~D);  // AND_Gate
  and and_3 (and_3_out, A, ~B);  // AND_Gate
  and and_4 (and_4_out, ~A, B);  // AND_Gate
  and and_5 (and_5_out, A, C);
  and and_6 (and_6_out, B, C, ~D);  // AND_Gate
  or or_1 (out_5, and_1_out, and_2_out, and_3_out, and_4_out, and_5_out, and_6_out);

  // Notes on the sheet:
  //   FEITO POR ARTHUR
endmodule

module Circuito_G (
  input  A,
  input  B,
  input  C,
  input  D,
  output out_5
);

  wire and_1_out, and_2_out, and_3_out, and_4_out, and_5_out;

  and and_1 (and_1_out, ~A, ~B, C);  // AND_Gate
  and and_2 (and_2_out, ~A, B, ~C);  // AND_Gate
  and and_3 (and_3_out, A, B, D);
  and and_4 (and_4_out, A, ~B);  // AND_Gate
  and and_5 (and_5_out, C, ~D);  // AND_Gate
  or or_1 (out_5, and_1_out, and_2_out, and_3_out, and_4_out, and_5_out);

  // Notes on the sheet:
  //   FEITO POR ARTHUR
endmodule

module Somador_com (
  input  A,
  input  B,
  input  Carry_In,
  output Sum,
  output Carry_Out
);

  wire and_1_out, and_2_out, and_3_out, xor_1_out;

  xor xor_1 (xor_1_out, A, B);
  and and_1 (and_1_out, B, Carry_In);
  and and_2 (and_2_out, A, Carry_In);
  and and_3 (and_3_out, A, B);
  xor xor_2 (Sum, xor_1_out, Carry_In);
  or or_1 (Carry_Out, and_1_out, and_2_out, and_3_out);
endmodule

module Somador (
  input  [3:0] New,
  input  in_2,
  input  [3:0] Chute,
  output [3:0] out_4
);

  wire Co0, Co1, Co2;

  Somador_com somador_com_1 (.A(New[3]), .B(Chute[3]), .Carry_In(Co2), .Sum(out_4[3]));  // open: Carry_Out
  Somador_com somador_com_2 (.A(New[2]), .B(Chute[2]), .Carry_In(Co1), .Sum(out_4[2]), .Carry_Out(Co2));
  Somador_com somador_com_3 (.A(New[1]), .B(Chute[1]), .Carry_In(Co0), .Sum(out_4[1]), .Carry_Out(Co1));
  Somador_com somador_com_4 (.A(New[0]), .B(Chute[0]), .Carry_In(in_2), .Sum(out_4[0]), .Carry_Out(Co0));

  // Other names for the same wires on the sheet: _0 = out_4[0]; _1 = out_4[1]; _2 = out_4[2]; _3 = out_4[3]
endmodule

module _1_a_4_bits (
  input  in_1,
  output [3:0] out_2
);


  assign out_2 = {4{in_1}};
endmodule

module _1_a_8_bits (
  input  in_1,
  output [7:0] out_2
);


  assign out_2 = {8{in_1}};
endmodule

module _4_a_8_bits (
  input  [3:0] in_1,
  output [7:0] out_2
);


  assign out_2 = {in_1, in_1};
endmodule

module Multiplexador (
  input  [3:0] in_1,
  input  [3:0] in_2,
  input  in_3,
  input  in_4,
  input  in_5,
  output [3:0] out_6
);

  wire or_1_out;
  wire [3:0] and_1_out, and_2_out, n1_a_4_bits_1_out_2, n1_a_4_bits_2_out_2;

  _1_a_4_bits u_1_a_4_bits_1 (.out_2(n1_a_4_bits_1_out_2), .in_1(or_1_out));
  or or_1 (or_1_out, in_3, in_4);
  _1_a_4_bits u_1_a_4_bits_2 (.out_2(n1_a_4_bits_2_out_2), .in_1(in_5));
  assign and_1_out = in_1 & n1_a_4_bits_1_out_2 & ~n1_a_4_bits_2_out_2;  // AND_Gate and_1, 4 bits wide
  assign out_6 = and_1_out | and_2_out;  // OR_Gate or_2, 4 bits wide
  assign and_2_out = in_2 & ~n1_a_4_bits_1_out_2 & n1_a_4_bits_2_out_2;  // AND_Gate and_2, 4 bits wide
endmodule

module \Diferença  (
  input  [3:0] A,
  input  [3:0] B,
  output [3:0] out_3
);

  wire comparador_de_magnitude_1_a___b, comparador_de_magnitude_1_a___b_2, comparador_de_magnitude_1_a___b_3;
  wire [3:0] not_1_out, not_2_out, somador_1_out_4, somador_2_out_4;

  Somador somador_1 (.New(A), .Chute(not_1_out), .out_4(somador_1_out_4), .in_2(1'b1));
  assign not_1_out = ~B;  // NOT_Gate not_1, 4 bits wide
  assign not_2_out = ~A;  // NOT_Gate not_2, 4 bits wide
  Somador somador_2 (.New(not_2_out), .Chute(B), .out_4(somador_2_out_4), .in_2(1'b1));
  Comparador_de_Magnitude comparador_de_magnitude_1 (
    .A(A), .B(B), .A___B(comparador_de_magnitude_1_a___b), .A___B_2(comparador_de_magnitude_1_a___b_2),
    .A___B_3(comparador_de_magnitude_1_a___b_3));
  Multiplexador multiplexador_1 (
    .in_1(somador_1_out_4), .out_6(out_3), .in_2(somador_2_out_4), .in_3(comparador_de_magnitude_1_a___b),
    .in_4(comparador_de_magnitude_1_a___b_2), .in_5(comparador_de_magnitude_1_a___b_3));
endmodule

module Comparador_de_Magnitude (
  input  [3:0] A,
  input  [3:0] B,
  output A___B,
  output A___B_2,
  output A___B_3
);

  wire and_1_out, and_2_out, and_3_out, and_4_out, and_5_out, and_6_out, and_8_out, and_9_out, xnor_1_out,
       xnor_2_out, xnor_3_out, xnor_4_out;

  xnor xnor_1 (xnor_1_out, A[3], B[3]);
  xnor xnor_2 (xnor_2_out, A[2], B[2]);
  xnor xnor_3 (xnor_3_out, A[1], B[1]);
  xnor xnor_4 (xnor_4_out, A[0], B[0]);
  and and_1 (and_1_out, A[3], ~B[3]);  // AND_Gate
  and and_2 (and_2_out, A[2], xnor_1_out, ~B[2]);  // AND_Gate
  and and_3 (and_3_out, B[2], xnor_1_out, ~A[2]);  // AND_Gate
  and and_4 (and_4_out, B[3], ~A[3]);  // AND_Gate
  and and_5 (and_5_out, A[1], xnor_1_out, xnor_2_out, ~B[1]);  // AND_Gate
  and and_6 (and_6_out, A[0], xnor_1_out, xnor_2_out, xnor_3_out, ~B[0]);  // AND_Gate
  and and_7 (A___B_2, xnor_1_out, xnor_2_out, xnor_3_out, xnor_4_out);
  and and_8 (and_8_out, B[0], xnor_3_out, xnor_2_out, xnor_1_out, ~A[0]);  // AND_Gate
  and and_9 (and_9_out, B[1], xnor_2_out, xnor_1_out, ~A[1]);  // AND_Gate
  or or_1 (A___B, and_1_out, and_2_out, and_5_out, and_6_out);
  or or_2 (A___B_3, and_8_out, and_9_out, and_3_out, and_4_out);

  // Notes on the sheet:
  //   FEITO POR ARTHUR
endmodule
